// Logisim project regfile.circ as structural Verilog: 1 circuit, main circuit main
module main (
  input  [4:0] Read_Register_1,
  input  [4:0] Read_Register_2,
  input  [4:0] Write_Register,
  input  [31:0] Write_Data,
  input  Write_Enable,
  input  Clock,
  output [31:0] s0_Value,
  output [31:0] s1_Value,
  output [31:0] s2_Value,
  output [31:0] ra_Value,
  output [31:0] sp_Value,
  output [31:0] Read_Data_1,
  output [31:0] Read_Data_2
);

  wire and_1_out, and_2_out, and_3_out, and_4_out, and_5_out, and_6_out, and_7_out, and_8_out, and_9_out,
       and_10_out, and_11_out, and_12_out, and_13_out, and_14_out, and_15_out, and_16_out, and_17_out,
       and_18_out, and_19_out, and_20_out, and_21_out, and_22_out, and_23_out, and_24_out, and_25_out,
       and_26_out, and_27_out, and_28_out, and_29_out, and_30_out, and_31_out, comparator_1_eq,
       comparator_2_eq, comparator_3_eq, comparator_4_eq, comparator_5_eq, comparator_6_eq, comparator_7_eq,
       comparator_8_eq, comparator_9_eq, comparator_10_eq, comparator_11_eq, comparator_12_eq,
       comparator_13_eq, comparator_14_eq, comparator_15_eq, comparator_16_eq, comparator_17_eq,
       comparator_18_eq, comparator_19_eq, comparator_20_eq, comparator_21_eq, comparator_22_eq,
       comparator_23_eq, comparator_24_eq, comparator_25_eq, comparator_26_eq, comparator_27_eq,
       comparator_28_eq, comparator_29_eq, comparator_30_eq, comparator_31_eq;
  wire [31:0] _0, _1, _2, _3, _4, _5, _6, _7, _8, _9, _10, _11, _12, _13, _14, _15, _19, _20, _21, _22, _23,
       _24, _25, _26, _27, _28, _30;

  Comparator #(.width(5), .mode("unsigned")) comparator_1 (
    .a(Write_Register), .b(5'b00011), .eq(comparator_1_eq));  // open: gt, lt
  Comparator #(.width(5), .mode("unsigned")) comparator_2 (
    .a(Write_Register), .b(5'b00110), .eq(comparator_2_eq));  // open: gt, lt
  Comparator #(.width(5), .mode("unsigned")) comparator_3 (
    .a(Write_Register), .b(5'b01001), .eq(comparator_3_eq));  // open: gt, lt
  Comparator #(.width(5), .mode("unsigned")) comparator_4 (
    .a(Write_Register), .b(5'b01100), .eq(comparator_4_eq));  // open: gt, lt
  Comparator #(.width(5), .mode("unsigned")) comparator_5 (
    .a(Write_Register), .b(5'b01111), .eq(comparator_5_eq));  // open: gt, lt
  Comparator #(.width(5), .mode("unsigned")) comparator_6 (
    .a(Write_Register), .b(5'b10010), .eq(comparator_6_eq));  // open: gt, lt
  Comparator #(.width(5), .mode("unsigned")) comparator_7 (
    .a(Write_Register), .b(5'b10101), .eq(comparator_7_eq));  // open: gt, lt
  Comparator #(.width(5), .mode("unsigned")) comparator_8 (
    .a(Write_Register), .b(5'b11000), .eq(comparator_8_eq));  // open: gt, lt
  Comparator #(.width(5), .mode("unsigned")) comparator_9 (
    .a(Write_Register), .b(5'b11011), .eq(comparator_9_eq));  // open: gt, lt
  Comparator #(.width(5), .mode("unsigned")) comparator_10 (
    .a(Write_Register), .b(5'b11110), .eq(comparator_10_eq));  // open: gt, lt
  Register #(.width(32)) register_1 (.D(Write_Data), .en(1'b0), .Q(_0), .clk(Clock), .clr(1'b1));
  Register #(.width(32)) register_2 (.D(Write_Data), .en(and_1_out), .Q(_3), .clk(Clock));  // open: clr
  and and_1 (and_1_out, comparator_1_eq, Write_Enable);
  Register #(.width(32)) register_3 (.D(Write_Data), .en(and_2_out), .Q(_6), .clk(Clock));  // open: clr
  and and_2 (and_2_out, comparator_2_eq, Write_Enable);
  Register #(.width(32)) register_4 (.D(Write_Data), .en(and_3_out), .Q(_9), .clk(Clock));  // open: clr
  and and_3 (and_3_out, comparator_3_eq, Write_Enable);
  Register #(.width(32)) register_5 (.D(Write_Data), .en(and_4_out), .Q(_12), .clk(Clock));  // open: clr
  and and_4 (and_4_out, comparator_4_eq, Write_Enable);
  Register #(.width(32)) register_6 (.D(Write_Data), .en(and_5_out), .Q(_15), .clk(Clock));  // open: clr
  and and_5 (and_5_out, comparator_5_eq, Write_Enable);
  Register #(.width(32)) register_7 (.D(Write_Data), .en(and_6_out), .Q(s2_Value), .clk(Clock));  // open: clr
  and and_6 (and_6_out, comparator_6_eq, Write_Enable);
  Register #(.width(32)) register_8 (.D(Write_Data), .en(and_7_out), .Q(_21), .clk(Clock));  // open: clr
  and and_7 (and_7_out, comparator_7_eq, Write_Enable);
  Register #(.width(32)) register_9 (.D(Write_Data), .en(and_8_out), .Q(_24), .clk(Clock));  // open: clr
  and and_8 (and_8_out, comparator_8_eq, Write_Enable);
  Register #(.width(32)) register_10 (.D(Write_Data), .en(and_9_out), .Q(_27), .clk(Clock));  // open: clr
  and and_9 (and_9_out, comparator_9_eq, Write_Enable);
  Register #(.width(32)) register_11 (.D(Write_Data), .en(and_10_out), .Q(_30), .clk(Clock));  // open: clr
  and and_10 (and_10_out, comparator_10_eq, Write_Enable);
  Multiplexer #(.select(5), .width(32)) multiplexer_1 (
    .in0(_0), .in1(_1), .in2(_2), .in3(_3), .in4(_4), .in5(_5), .in6(_6), .in7(_7), .in8(_8), .in9(_9),
    .in10(_10), .in11(_11), .in12(_12), .in13(_13), .in14(_14), .in15(_15), .in16(s0_Value), .in17(s1_Value),
    .in18(s2_Value), .in19(_19), .in20(_20), .in21(_21), .in22(_22), .in23(_23), .in24(_24), .in25(_25),
    .in26(_26), .in27(_27), .in28(_28), .in29(sp_Value), .in30(_30), .in31(ra_Value), .out(Read_Data_1),
    .sel(Read_Register_1));  // open: en
  Comparator #(.width(5), .mode("unsigned")) comparator_11 (
    .a(Write_Register), .b(5'b00001), .eq(comparator_11_eq));  // open: gt, lt
  Comparator #(.width(5), .mode("unsigned")) comparator_12 (
    .a(Write_Register), .b(5'b00100), .eq(comparator_12_eq));  // open: gt, lt
  Comparator #(.width(5), .mode("unsigned")) comparator_13 (
    .a(Write_Register), .b(5'b00111), .eq(comparator_13_eq));  // open: gt, lt
  Comparator #(.width(5), .mode("unsigned")) comparator_14 (
    .a(Write_Register), .b(5'b01010), .eq(comparator_14_eq));  // open: gt, lt
  Comparator #(.width(5), .mode("unsigned")) comparator_15 (
    .a(Write_Register), .b(5'b01101), .eq(comparator_15_eq));  // open: gt, lt
  Comparator #(.width(5), .mode("unsigned")) comparator_16 (
    .a(Write_Register), .b(5'b10000), .eq(comparator_16_eq));  // open: gt, lt
  Comparator #(.width(5), .mode("unsigned")) comparator_17 (
    .a(Write_Register), .b(5'b10011), .eq(comparator_17_eq));  // open: gt, lt
  Comparator #(.width(5), .mode("unsigned")) comparator_18 (
    .a(Write_Register), .b(5'b10110), .eq(comparator_18_eq));  // open: gt, lt
  Comparator #(.width(5), .mode("unsigned")) comparator_19 (
    .a(Write_Register), .b(5'b11001), .eq(comparator_19_eq));  // open: gt, lt
  Comparator #(.width(5), .mode("unsigned")) comparator_20 (
    .a(Write_Register), .b(5'b11100), .eq(comparator_20_eq));  // open: gt, lt
  Comparator #(.width(5), .mode("unsigned")) comparator_21 (
    .a(Write_Register), .b({5{1'b1}}), .eq(comparator_21_eq));  // open: gt, lt
  and and_11 (and_11_out, comparator_11_eq, Write_Enable);
  and and_12 (and_12_out, comparator_12_eq, Write_Enable);
  and and_13 (and_13_out, comparator_13_eq, Write_Enable);
  and and_14 (and_14_out, comparator_14_eq, Write_Enable);
  and and_15 (and_15_out, comparator_15_eq, Write_Enable);
  and and_16 (and_16_out, comparator_16_eq, Write_Enable);
  and and_17 (and_17_out, comparator_17_eq, Write_Enable);
  and and_18 (and_18_out, comparator_18_eq, Write_Enable);
  and and_19 (and_19_out, comparator_19_eq, Write_Enable);
  and and_20 (and_20_out, comparator_20_eq, Write_Enable);
  and and_21 (and_21_out, comparator_21_eq, Write_Enable);
  Register #(.width(32)) register_12 (.D(Write_Data), .en(and_11_out), .Q(_1), .clk(Clock));  // open: clr
  Register #(.width(32)) register_13 (.D(Write_Data), .en(and_12_out), .Q(_4), .clk(Clock));  // open: clr
  Register #(.width(32)) register_14 (.D(Write_Data), .en(and_13_out), .Q(_7), .clk(Clock));  // open: clr
  Register #(.width(32)) register_15 (.D(Write_Data), .en(and_14_out), .Q(_10), .clk(Clock));  // open: clr
  Register #(.width(32)) register_16 (.D(Write_Data), .en(and_15_out), .Q(_13), .clk(Clock));  // open: clr
  Register #(.width(32)) register_17 (.D(Write_Data), .en(and_16_out), .Q(s0_Value), .clk(Clock));  // open: clr
  Register #(.width(32)) register_18 (.D(Write_Data), .en(and_17_out), .Q(_19), .clk(Clock));  // open: clr
  Register #(.width(32)) register_19 (.D(Write_Data), .en(and_18_out), .Q(_22), .clk(Clock));  // open: clr
  Register #(.width(32)) register_20 (.D(Write_Data), .en(and_19_out), .Q(_25), .clk(Clock));  // open: clr
  Register #(.width(32)) register_21 (.D(Write_Data), .en(and_20_out), .Q(_28), .clk(Clock));  // open: clr
  Register #(.width(32)) register_22 (.D(Write_Data), .en(and_21_out), .Q(ra_Value), .clk(Clock));  // open: clr
  Multiplexer #(.select(5), .width(32)) multiplexer_2 (
    .in0(_0), .in1(_1), .in2(_2), .in3(_3), .in4(_4), .in5(_5), .in6(_6), .in7(_7), .in8(_8), .in9(_9),
    .in10(_10), .in11(_11), .in12(_12), .in13(_13), .in14(_14), .in15(_15), .in16(s0_Value), .in17(s1_Value),
    .in18(s2_Value), .in19(_19), .in20(_20), .in21(_21), .in22(_22), .in23(_23), .in24(_24), .in25(_25),
    .in26(_26), .in27(_27), .in28(_28), .in29(sp_Value), .in30(_30), .in31(ra_Value), .out(Read_Data_2),
    .sel(Read_Register_2));  // open: en
  Comparator #(.width(5), .mode("unsigned")) comparator_22 (
    .a(Write_Register), .b(5'b00010), .eq(comparator_22_eq));  // open: gt, lt
  and and_22 (and_22_out, comparator_22_eq, Write_Enable);
  Comparator #(.width(5), .mode("unsigned")) comparator_23 (
    .a(Write_Register), .b(5'b00101), .eq(comparator_23_eq));  // open: gt, lt
  and and_23 (and_23_out, comparator_23_eq, Write_Enable);
  Comparator #(.width(5), .mode("unsigned")) comparator_24 (
    .a(Write_Register), .b(5'b01000), .eq(comparator_24_eq));  // open: gt, lt
  and and_24 (and_24_out, comparator_24_eq, Write_Enable);
  Comparator #(.width(5), .mode("unsigned")) comparator_25 (
    .a(Write_Register), .b(5'b01011), .eq(comparator_25_eq));  // open: gt, lt
  and and_25 (and_25_out, comparator_25_eq, Write_Enable);
  Comparator #(.width(5), .mode("unsigned")) comparator_26 (
    .a(Write_Register), .b(5'b01110), .eq(comparator_26_eq));  // open: gt, lt
  and and_26 (and_26_out, comparator_26_eq, Write_Enable);
  Comparator #(.width(5), .mode("unsigned")) comparator_27 (
    .a(Write_Register), .b(5'b10001), .eq(comparator_27_eq));  // open: gt, lt
  and and_27 (and_27_out, comparator_27_eq, Write_Enable);
  Comparator #(.width(5), .mode("unsigned")) comparator_28 (
    .a(Write_Register), .b(5'b10100), .eq(comparator_28_eq));  // open: gt, lt
  and and_28 (and_28_out, comparator_28_eq, Write_Enable);
  Comparator #(.width(5), .mode("unsigned")) comparator_29 (
    .a(Write_Register), .b(5'b10111), .eq(comparator_29_eq));  // open: gt, lt
  and and_29 (and_29_out, comparator_29_eq, Write_Enable);
  Comparator #(.width(5), .mode("unsigned")) comparator_30 (
    .a(Write_Register), .b(5'b11010), .eq(comparator_30_eq));  // open: gt, lt
  and and_30 (and_30_out, comparator_30_eq, Write_Enable);
  Comparator #(.width(5), .mode("unsigned")) comparator_31 (
    .a(Write_Register), .b(5'b11101), .eq(comparator_31_eq));  // open: gt, lt
  and and_31 (and_31_out, comparator_31_eq, Write_Enable);
  Register #(.width(32)) register_23 (.D(Write_Data), .en(and_22_out), .Q(_2), .clk(Clock));  // open: clr
  Register #(.width(32)) register_24 (.D(Write_Data), .en(and_23_out), .Q(_5), .clk(Clock));  // open: clr
  Register #(.width(32)) register_25 (.D(Write_Data), .en(and_24_out), .Q(_8), .clk(Clock));  // open: clr
  Register #(.width(32)) register_26 (.D(Write_Data), .en(and_25_out), .Q(_11), .clk(Clock));  // open: clr
  Register #(.width(32)) register_27 (.D(Write_Data), .en(and_26_out), .Q(_14), .clk(Clock));  // open: clr
  Register #(.width(32)) register_28 (.D(Write_Data), .en(and_27_out), .Q(s1_Value), .clk(Clock));  // open: clr
  Register #(.width(32)) register_29 (.D(Write_Data), .en(and_28_out), .Q(_20), .clk(Clock));  // open: clr
  Register #(.width(32)) register_30 (.D(Write_Data), .en(and_29_out), .Q(_23), .clk(Clock));  // open: clr
  Register #(.width(32)) register_31 (.D(Write_Data), .en(and_30_out), .Q(_26), .clk(Clock));  // open: clr
  Register #(.width(32)) register_32 (.D(Write_Data), .en(and_31_out), .Q(sp_Value), .clk(Clock));  // open: clr

  // Other names for the same wires on the sheet: _16[31:0] = s0_Value; _17[31:0] = s1_Value; _18[31:0] = s2_Value;
  //   _29[31:0] = sp_Value; _31[31:0] = ra_Value; clk = Clock; read_data1[31:0] = Read_Data_1;
  //   read_data2[31:0] = Read_Data_2; read_reg1[4:0] = Read_Register_1; read_reg2[4:0] = Read_Register_2;
  //   write_en = Write_Enable; write_reg[4:0] = Write_Register

  // Notes on the sheet:
  //   INPUTS to your circuit
  //   DON'T CHANGE THE LOCATIONS OF THE INPUTS AND OUTPUTS!
  //   These are DEBUG/TEST outputs from your circuit.
  //   OUTPUTS from your circuit
endmodule
